# Fritzing sketch project2 (saved by Fritzing 0.9.3b)
breadboards: 1

parts:
  Part1 = Arduino Yun
  LED1 = smd LED [color="Red (633nm)" package="0603 [SMD]"]
  S1 = Pushbutton [package="[SMD]"]
  R1 = Resistor [tolerance=±5% resistance=10k package=THT]
  U1 = TMP36 [package=to-92]
  R2 = Resistor [tolerance=±5% resistance=10k package=THT]

nets:
  N1: Part1.A0, U1.VOUT
  N2: Part1.D13/SCK, LED1.anode
  GND: Part1.GND, R1.Pin_0, U1.GND, R2.Pin_0
  N3: Part1.D3_PWM, S1.Pin_1, S1.Pin_2
  5V: Part1.5V, S1.Pin_3, S1.Pin_4, U1.VCC, R2.Pin_1
  N4: LED1.cathode, R1.Pin_1
